# Fritzing sketch RadBit (saved by Fritzing 0.9.3b)

parts:
  IC1 = Teviso RD3024 [chip_label=IC]
  Part2 = Adafruit DS3231 [part_number="Adafruit #3013"]
  Part3 = SPI Non-Volatile FRAM 8KB
  Part1 = LightBlue Bean+

nets:
  N1: IC1.OUT, Part1.D0
  VCC: IC1.VCC, Part2.Vin, Part3.VCC, Part1.3.3V
  GND: IC1.GND, Part2.GND, Part3.GND, Part1.GND, Part1.Grove_A2/A3
  N2: Part2.SCL, Part1.A5/SCL
  N3: Part2.SDA, Part1.A4/SDA
  N4: Part3.CS, Part1.D6/SS
  N5: Part3.MOSI, Part1.D7/MOSI
  N6: Part3.MISO, Part1.D8/MISO
  N7: Part3.SCK, Part1.D9/SCK

custom parts:
  Teviso RD3024: A low voltage solid state radiation sensor, in combination with high immunity to RF fields make it a good choice for new state-of-the-art designs of battery powered applications using WiFi, GSM and Bluetooth communication.
  Adafruit DS3231: The datasheet for the DS3231 explains that this part is an "Extremely Accurate I²C-Integrated RTC/TCXO/Crystal". And, hey, it does exactly what it says on the tin! This Real Time Clock (RTC) is the most precise you can get in a small, low power package. Most RTCs use an external 32kHz timing crystal that is used to keep time with low current draw. And that's all well and good, but those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
  SPI Non-Volatile FRAM 8KB: With our SPI FRAM breakout board you can add some FRAM storage to your next DIY project. FRAM allows for a lower power usage and a faster write performance. It's excellent for low-power or inconsistent-power datalogging or data buffering where you want to stream data fast while also keeping the data when there's no power. Unlike Flash or EEPROM there's no pages to worry about. Each byte can be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
  LightBlue Bean+: http://store.punchthrough.com/collections/all/products/lightblue-bean-plus
